# Fritzing sketch StratoBalloon (saved by Fritzing 0.9.3b)
perfboards: 2

parts:
  Grove1 = Grove OLED 128x96  # not connected
  Raspberry_Pi_Zero1 = Raspberry Pi Zero  # not connected
  S1 = Round Pushbutton  # not connected
  U1 = TEMPERATURE-SENSOR [package=to-92]
  S2 = Pushbutton [package="[THT]"]  # not connected
  RHT1 = Humidity and Temperature Sensor RHT03
  VCC1 = Battery  # not connected
  LED1 = LED - 3mm [color="Red (633nm)" package="3 mm [THT]"]  # not connected
  X1 = USB Connectors [package=usb-microb]  # not connected
  U5 = Mini-USB _B_ connector with 5th pin broken out. [package=usb-minib]  # not connected
  U8 = LCD-16X2 [package=lcd-8x2-kit]  # not connected
  R1 = Resistor [tolerance=±5% resistance=220 package=THT]
  R2 = Resistor [tolerance=±5% resistance=220 package=THT]
  R3 = Resistor [tolerance=±5% resistance=220 package=THT]
  R4 = Resistor [tolerance=±5% resistance=220 package=THT]
  J2 = shrouded pin header, 40 pins [form="♂ (shrouded male)"]  # not connected

nets:
  N1: U1.GND, RHT1.GND_2
  N2: U1.ADJ, RHT1.Vcc, R1.Pin_1, R2.Pin_1
  N3: U1.VCC, R2.Pin_0
  N4: RHT1.Data-signal, R1.Pin_0
  N5: R3.Pin_1, R4.Pin_1
